// Digital circuit arith.dig as structural Verilog
module arith (
  input  [3:0] a,
  input  [3:0] b,
  input  ci,
  input  sel,
  output [3:0] S,
  output CO,
  output [3:0] D,
  output BO,
  output GT,
  output EQ,
  output LT,
  output SLT,
  output [3:0] M,
  output [3:0] N,
  output [5:0] E,
  output D2,
  output [3:0] DM1
);

  Add #(.Bits(4)) add_1 (.a(a), .b(b), .c_i(ci), .s(S), .c_o(CO));
  Sub #(.Bits(4)) sub_1 (.a(a), .b(b), .c_i(ci), .s(D), .c_o(BO));
  Comparator #(.Bits(4)) comparator_1 (.a(a), .b(b), .gt(GT), .eq(EQ), .lt(LT));
  Multiplexer #(.Bits(4)) multiplexer_1 (.sel(sel), .in_0(a), .in_1(b), .out(M));
  Neg #(.Bits(4)) neg_1 (.in(a), .out(N));
  Decoder #(.Selector_Bits(2)) decoder_1 (.sel(a[1:0]), .out_1(D2));  // open: out_0, out_2, out_3
  Comparator #(.Bits(4), .Signed("true")) comparator_2 (.a(a), .b(b), .lt(SLT));  // open: gt, eq
  BitExtender #(.inputBits(4), .outputBits(6)) bitextender_1 (.in(a), .out(E));
  Demultiplexer #(.Bits(4)) demultiplexer_1 (.sel(sel), .in(b), .out_1(DM1));  // open: out_0
  // Pins of 1 and 4 bits meet at S
  // Pins of 1 and 4 bits meet at D
  // Pins of 1 and 4 bits meet at M
  // Pins of 1 and 4 bits meet at N
  // Pins of 1 and 6 bits meet at E
  // Pins of 1 and 4 bits meet at DM1

  // Other names for the same wires on the sheet: sel2[1:0] = a[1:0]
endmodule
