// Logisim project bus.circ as structural Verilog: 1 circuit, main circuit main
module main (
  input  [3:0] X,
  output [3:0] Y,
  output [3:0] Y2
);

  assign Y2 = X & 4'b0101;  // AND_Gate and_1, 4 bits wide
  // Probe on nothing

  assign Y = {X[0], X[1], X[2], X[3]};

  // Other names for the same wires on the sheet: b3 = X[3]; b2 = X[2]; b1 = X[1]; b0 = X[0]
endmodule
