// Logisim project counter.circ as structural Verilog: 1 circuit, main circuit counter
module counter (
  output Q0,
  output Q1
);

  wire clock_1_out, d_ff_1_qn, xor_1_out;

  Clock clock_1 (.out(clock_1_out));
  D_Flip_Flop d_ff_1 (.D(d_ff_1_qn), .clk(clock_1_out), .Q(Q0), .Qn(d_ff_1_qn));  // open: preset, reset
  D_Flip_Flop d_ff_2 (.D(xor_1_out), .clk(clock_1_out), .Q(Q1));  // open: Qn, preset, reset
  xor xor_1 (xor_1_out, Q0, Q1);
endmodule
