// Digital circuit counter2.dig as structural Verilog
module counter2 (
  input  C,
  output Q0,
  output Q1
);

  wire ff0_nq, undriven, undriven_2, undriven_3, xor_1_out;

  xor xor_1 (xor_1_out, undriven_2, undriven_3);
  D_FF ff0 (.D(ff0_nq), .C(C), .Q(Q0), .nQ(ff0_nq));
  D_FF ff1 (.D(xor_1_out), .C(undriven), .Q(Q1));  // open: nQ
endmodule

/* Test case counts:
C Q1 Q0
0 0 0
C 0 1
C 1 0
C 1 1
C 0 0
*/
