// Logisim project fulladder.circ as structural Verilog: 2 circuits, main circuit full_adder
module full_adder (
  input  A,
  input  B,
  input  Cin,
  output Cout,
  output Sum
);

  wire ha1_c, ha1_s, ha2_c;

  half_adder ha1 (.A(A), .B(B), .S(ha1_s), .C(ha1_c));
  half_adder ha2 (.A(ha1_s), .B(Cin), .S(Sum), .C(ha2_c));
  or or_1 (Cout, ha1_c, ha2_c);
endmodule

module half_adder (
  input  A,
  input  B,
  output S,
  output C
);

  xor xor_1 (S, A, B);
  and and_1 (C, A, B);
endmodule
