// Digital circuit gates.dig as structural Verilog
module gates (
  input  a,
  input  b,
  input  c,
  output Y1,
  output Y2,
  output Y3,
  output Y4,
  output Y5
);

  and and_1 (Y1, a, ~b, c);  // And
  nand nand_1 (Y2, a, b, c);
  xor xor_1 (Y3, a, b, c);
  nor nor_1 (Y4, a, c);
  not not_1 (Y5, b);
endmodule
