// Logisim project halfadder.circ as structural Verilog: 1 circuit, main circuit half_adder
module half_adder (
  input  A,
  input  B,
  output S,
  output C
);

  xor xor_1 (S, A, B);
  and and_1 (C, A, B);

  // Notes on the sheet:
  //   Half adder
endmodule
