// Logisim project old27.circ as structural Verilog: 1 circuit, main circuit main
module main (
  input  I0,
  input  I1,
  input  S,
  input  P,
  input  Q,
  output Y,
  output PQ
);

  Multiplexer multiplexer_1 (.in0(I0), .in1(I1), .out(Y), .sel(S));  // open: en
  and and_1 (PQ, P, Q);
endmodule
