// Digital circuit ram.dig as structural Verilog
module ram (
  input  [1:0] A,
  input  [3:0] Din,
  input  str,
  input  C,
  input  ld,
  output [3:0] D
);

  RAMDualPort #(.AddrBits(2), .Bits(4)) ramdualport_1 (.A(A), .Din(Din), .str(str), .C(C), .ld(ld), .D(D));
  // Pins of 1 and 4 bits meet at D
endmodule
