// Digital circuit reverse4.dig as structural Verilog
module reverse4 (
  input  [3:0] X,
  output [3:0] Y,
  output [3:0] Z,
  output [1:0] H,
  output L0
);

  assign Z = X & {X[0], X[1], X[2], X[3]};  // And and_1, 4 bits wide
  // Pins of 1 and 4 bits meet at Z
  // Pins of 1 and 2 bits meet at X[3:2]

  assign H = X[3:2];
  assign L0 = X[0];
  assign Y = {X[0], X[1], X[2], X[3]};

  // Other names for the same wires on the sheet: b0 = X[0]; xin[3:0] = X; yout[3:0] = {X[0], X[1], X[2], X[3]};
  //   b1 = X[1]; b2 = X[2]; b3 = X[3]
endmodule
