// Logisim project rom.circ as structural Verilog: 1 circuit, main circuit main
module main (
  input  [1:0] A,
  output [3:0] D
);

  ROM #(.addrWidth(2), .dataWidth(4)) rom_1 (.addr(A), .data(D));
  Joystick joystick_1 (.x(D));  // open: y
  Hex_Digit_Display hex_digit_display_1 (.value(D));  // open: dp

  // Notes on the sheet:
  //   contents of rom_1 (hex, n*v repeats v):
  //   3 5 a f
endmodule
