// Digital circuit seq.dig as structural Verilog
module seq (
  input  clk,
  input  en,
  input  clr,
  input  [3:0] d,
  input  [2:0] A,
  output [2:0] Q,
  output OVF,
  output [3:0] R,
  output [3:0] ROMD
);

  Counter #(.Bits(3)) counter_1 (.en(en), .C(clk), .clr(clr), .out(Q), .ovf(OVF));
  Register #(.Bits(4)) register_1 (.D(d), .C(clk), .en(en), .Q(R));
  ROM #(.AddrBits(3), .Bits(4)) rom_1 (.A(A), .D(ROMD));  // open: sel
  // Pins of 1 and 3 bits meet at Q
  // Pins of 1 and 4 bits meet at R
  // Pins of 1 and 4 bits meet at ROMD

  // Notes on the sheet:
  //   contents of rom_1 (hex, n*v repeats v):
  //   5,a,3*f
endmodule
