// Digital circuit unknown.dig as structural Verilog
module unknown (
  input  [3:0] A,
  input  [3:0] B,
  input  X,
  output [7:0] P,
  output Y
);

  wire missing_1_p2;

  Mul #(.Bits(4)) mul_1 (.a(A), .b(B), .mul(P));
  // missing missing_1: pin names not known; wires that end beside it: X, missing_1_p2, Y
  // Probe on missing_1_p2
  // Pins of 1 and 8 bits meet at P
endmodule
